# Fritzing sketch Wiring (saved by Fritzing 0.9.3b)
# 18650 Li-ion Battery: CC-BY Dr Kristofer Chan, King's College London/Remote-research.org
breadboards: 2

parts:
  R1 = Basic Flex Resistor
  R2 = Basic Flex Resistor
  U2 = Vibration Motor- ROB-08449 [package=vibe-motor-10mm]
  U3 = Vibration Motor- ROB-08449 [package=vibe-motor-10mm]
  U4 = Vibration Motor- ROB-08449 [package=vibe-motor-10mm]
  U5 = Vibration Motor- ROB-08449 [package=vibe-motor-10mm]
  J1 = Piezo Speaker
  LED2 = smd LED [color="Red (633nm)" package="1206 [SMD]"]
  LED3 = smd LED [color="Red (633nm)" package="1206 [SMD]"]
  S1 = Round Pushbutton
  R3 = Resistor [tolerance=±5% resistance=220 package="2512 [SMD]"]
  R5 = Resistor [tolerance=±5% resistance=220 package="2512 [SMD]"]
  R6 = Basic Flex Resistor
  R7 = Basic Flex Resistor
  R8 = Resistor [tolerance=±5% resistance=220 package="2010 [SMD]"]
  R9 = Resistor [tolerance=±5% resistance=220 package="2010 [SMD]"]
  R10 = Resistor [tolerance=±5% resistance=220 package="2010 [SMD]"]
  R11 = Resistor [tolerance=±5% resistance=220 package="2010 [SMD]"]
  U1 = ESP32S-HiLetgo [part_number=ESP32S-HiLetgo]
  LED4 = smd LED [color="Red (633nm)" package="1206 [SMD]"]
  S2 = Round Pushbutton
  M1 = AC-05-03
  BAT1 = 18650 Li-ion Battery [package=battery-18650]
  BAT2 = 18650 Li-ion Battery [package=battery-18650]
  BAT3 = 18650 Li-ion Battery [package=battery-18650]
  BAT4 = 18650 Li-ion Battery [package=battery-18650]
  M2 = tp5100 [package=THT]
  J2 = Basic Force Sensing Resistor (FSR) [package=THT]
  J3 = Basic Force Sensing Resistor (FSR) [package=THT]
  J4 = Basic Force Sensing Resistor (FSR) [package=THT]
  J5 = Basic Force Sensing Resistor (FSR) [package=THT]
  R12 = Resistor [tolerance=±5% resistance=220 package="2010 [SMD]"]
  R13 = Resistor [tolerance=±5% resistance=220 package="2010 [SMD]"]
  R14 = Resistor [tolerance=±5% resistance=220 package="2010 [SMD]"]
  R15 = Resistor [tolerance=±5% resistance=220 package="2010 [SMD]"]
  R4 = Resistor [tolerance=±5% resistance=220 package="2512 [SMD]"]

nets:
  N1: R1.pin_1, R2.pin_1, R6.pin_1, R7.pin_1
  N2: U2.+, U3.+, U4.+, U5.+, J1.pin1, M1.pin_4, BAT3.-, BAT4.-, M2.-IN, M2.-BAT, J2.pin_0, J3.pin_0, J4.pin_0, J5.pin_0
  N3: U2.-, U1.GPIO13
  N4: U3.-, U1.GPIO14
  N5: U4.-, U1.GPIO18
  N6: U5.-, U1.GPIO19
  N7: J1.pin2, U1.GPIO23
  N8: LED2.cathode, R4.Pin_0, R4.Pin_1
  N9: LED2.anode, U1.GPIO27
  N10: LED3.cathode, R5.Pin_0, R5.Pin_1
  N11: LED3.anode, U1.GPIO4
  N12: S1.leg1, U1.GPIO16
  N13: R3.Pin_0, R3.Pin_1, U1.GPIO12, LED4.cathode
  N14: R8.Pin_0, U1.GPIO35
  N15: R8.Pin_1, R9.Pin_1, R10.Pin_1, R11.Pin_1, U1.3.3, U1.GND, LED4.anode, BAT1.+, BAT2.+, M2.+BAT, R12.Pin_1, R13.Pin_1, R14.Pin_1, R15.Pin_1
  N16: R9.Pin_0, U1.GPIO34
  N17: R10.Pin_0, U1.GPIO39
  N18: R11.Pin_0, U1.GPIO36
  N19: U1.GPIO32, J2.pin_1
  N20: U1.GPIO33, J3.pin_1
  N21: U1.GPIO25, J4.pin_1
  N22: U1.GPIO26, J5.pin_1
  N23: U1.GPIO17, S2.leg1
  N24: M1.pin_3, M2.+_IN
  N25: BAT1.-, BAT2.-, BAT3.+, BAT4.+

custom parts:
  ESP32S-HiLetgo: HiLetgo ESP-WROOM-32 ESP32 ESP-32S Development Board 2.4GHz Dual-Mode WiFi + Bluetooth Dual Cores Microcontroller The ESP32 integrated with Antenna switches, RF Balun, power amplifiers, low-noise amplifiers, filters, and management modules, and the entire solution occupies the least area of PCB. 2.4 GHz Wi-Fi plus Bluetooth dual-mode chip, with TSMC Ultra-low power consumption 40nm technology,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
  AC-05-03: AC-DC 220V to 5V Step-Down Power Supply Module
  18650 Li-ion Battery: 18650 li-ion Battery Standard 18650 battery with interactive connectors Creative Common Attribution 4.0 International (CC-BY 4.0) license. Any use of this part requires attribution of Dr Kristofer Chan, Department of Geography, King's College London. Contact kristofer.chan [at] kcl.ac.uk OR kris [at] remote-research.org for further information.
  tp5100: Tp5100 battery charger module. Generic ebay type.
